// Logisim project MIC-1.circ as structural Verilog: 19 circuits, main circuit main
module main (
  input  CLK,
  output [31:0] PC,
  output [8:0] MPC,
  output [31:0] B,
  output [31:0] C
);

  wire control_unit_1_cpp_b, control_unit_1_cpp_c, control_unit_1_h_c, control_unit_1_lv_b,
       control_unit_1_lv_c, control_unit_1_mar_c, control_unit_1_mbr_b, control_unit_1_mbru_b,
       control_unit_1_mdr_b, control_unit_1_mdr_c, control_unit_1_opc_b, control_unit_1_opc_c,
       control_unit_1_pc_b, control_unit_1_pc_c, control_unit_1_sp_b, control_unit_1_sp_c,
       control_unit_1_tos_b, control_unit_1_tos_c, data_path_1_n, data_path_1_z, RESET_out;
  wire [1:0] control_unit_1_alu_2, control_unit_1_shifter;
  wire [2:0] control_unit_1_mem;
  wire [3:0] control_unit_1_alu;
  wire [7:0] data_path_1_op_code, mem_1_mem_fetch;
  wire [31:0] data_path_1_mem_mar, data_path_1_mem_wr, mem_1_mrm_rd;

  Mem mem_1 (
    .MEM_ADDR_32(data_path_1_mem_mar), .CLK(CLK), .MEM_WR(data_path_1_mem_wr), .MRM_RD(mem_1_mrm_rd),
    .MEM_FETCH(mem_1_mem_fetch), .wr(control_unit_1_mem[2]), .rd(control_unit_1_mem[1]),
    .fetch(control_unit_1_mem[0]), .MEM_ADDR_8(PC));
  Button RESET (.out(RESET_out));
  Data_Path data_path_1 (
    .MEM_WR(data_path_1_mem_wr), .MEM_RD(mem_1_mrm_rd), .rd(control_unit_1_mem[1]),
    .MEM_FETCH(mem_1_mem_fetch), .RESET(RESET_out), .INVA(control_unit_1_alu[1]),
    .ENA(control_unit_1_alu[3]), .CLK(CLK), .ENB(control_unit_1_alu[2]), .INC(control_unit_1_alu[0]),
    .F(control_unit_1_alu_2), .SRA1(control_unit_1_shifter[0]), .SLL8(control_unit_1_shifter[1]),
    .MEM_MAR(data_path_1_mem_mar), .OP_CODE(data_path_1_op_code), .N(data_path_1_n), .Z(data_path_1_z),
    .MAR_C(control_unit_1_mar_c), .MDR_C(control_unit_1_mdr_c), .PC_C(control_unit_1_pc_c),
    .fetch(control_unit_1_mem[0]), .SP_C(control_unit_1_sp_c), .LV_C(control_unit_1_lv_c),
    .CPP_C(control_unit_1_cpp_c), .TOS_C(control_unit_1_tos_c), .OPC_C(control_unit_1_opc_c),
    .H_C(control_unit_1_h_c), .MBR(control_unit_1_mbr_b), .MBRU(control_unit_1_mbru_b),
    .MDR_B(control_unit_1_mdr_b), .PC_B(control_unit_1_pc_b), .SP_B(control_unit_1_sp_b),
    .LV_B(control_unit_1_lv_b), .CPP_B(control_unit_1_cpp_b), .TOS_B(control_unit_1_tos_b),
    .OPC_B(control_unit_1_opc_b), .MEM_PC(PC), .B(B), .C(C));
  Control_Unit control_unit_1 (
    .CLK(CLK), .RESET(RESET_out), .MBR(data_path_1_op_code), .N(data_path_1_n), .Z(data_path_1_z), .MPC(MPC),
    .MDR_B(control_unit_1_mdr_b), .PC_B(control_unit_1_pc_b), .MBR_B(control_unit_1_mbr_b),
    .MBRU_B(control_unit_1_mbru_b), .SP_B(control_unit_1_sp_b), .LV_B(control_unit_1_lv_b),
    .CPP_B(control_unit_1_cpp_b), .TOS_B(control_unit_1_tos_b), .OPC_B(control_unit_1_opc_b),
    .Mem(control_unit_1_mem), .ALU({control_unit_1_alu_2, control_unit_1_alu}),
    .Shifter(control_unit_1_shifter), .H_C(control_unit_1_h_c), .OPC_C(control_unit_1_opc_c),
    .TOS_C(control_unit_1_tos_c), .CPP_C(control_unit_1_cpp_c), .LV_C(control_unit_1_lv_c),
    .SP_C(control_unit_1_sp_c), .PC_C(control_unit_1_pc_c), .MDR_C(control_unit_1_mdr_c),
    .MAR_C(control_unit_1_mar_c));
endmodule

module Mem (
  input  wr,
  input  [31:0] MEM_WR,
  input  [31:0] MEM_ADDR_32,
  input  rd,
  input  [31:0] MEM_ADDR_8,
  input  fetch,
  input  CLK,
  output [31:0] MRM_RD,
  output [7:0] MEM_FETCH
);

  wire not_1_out, not_2_out, not_3_out;
  wire [7:0] ram_2_data;
  wire [31:0] ram_1_data;

  not not_1 (not_1_out, CLK);
  not not_2 (not_2_out, wr);
  RAM #(.addrWidth(24), .dataWidth(32)) ram_1 (
    .addr(MEM_ADDR_32[23:0]), .data(ram_1_data), .sel(1'b1), .clk(not_1_out), .ld(not_2_out), .clr(1'b0));
  assign ram_1_data = wr ? MEM_WR : 32'bz;  // Controlled_Buffer controlled_buffer_1
  assign MRM_RD = rd ? ram_1_data : 32'bz;  // Controlled_Buffer controlled_buffer_2
  not not_3 (not_3_out, CLK);
  RAM #(.addrWidth(24)) ram_2 (
    .addr(MEM_ADDR_8[23:0]), .data(ram_2_data), .sel(1'b1), .clk(not_3_out), .clr(1'b0));  // open: ld
  assign MEM_FETCH = fetch ? ram_2_data : 8'bz;  // Controlled_Buffer controlled_buffer_3

  // Notes on the sheet:
  //   Una truchada porque Logisim no tiene
  //   un bloque de memoria con dos canales de datos
endmodule

module Control_Unit (
  input  CLK,
  input  RESET,
  input  [7:0] MBR,
  input  N,
  input  Z,
  output [8:0] MPC,
  output MDR_B,
  output PC_B,
  output MBR_B,
  output MBRU_B,
  output SP_B,
  output LV_B,
  output CPP_B,
  output TOS_B,
  output OPC_B,
  output [2:0] Mem,
  output [5:0] ALU,
  output [1:0] Shifter,
  output H_C,
  output OPC_C,
  output TOS_C,
  output CPP_C,
  output LV_C,
  output SP_C,
  output PC_C,
  output MDR_C,
  output MAR_C
);

  wire and_1_out, and_2_out, d_flipflop_asc_1_q, d_flipflop_asc_2_q, not_1_out;
  wire [2:0] mir_1_jam;
  wire [3:0] control_store_1_cs_s4, mir_1_b;
  wire [7:0] mir_1_addr, multiplexer_3_out, or_2_out;
  wire [8:0] multiplexer_1_out, multiplexer_2_out;
  wire [8:8] mir_1_addr_2, or_1_out;
  wire [31:0] control_store_1_cs_s32;

  Multiplexer #(.width(9), .enable("false")) multiplexer_1 (
    .in0({9{1'b1}}), .in1(9'hff), .out(multiplexer_1_out), .sel(RESET));
  Multiplexer #(.width(9), .enable("false")) multiplexer_2 (
    .in0({9{1'b1}}), .in1(9'h100), .out(multiplexer_2_out), .sel(RESET));
  and and_1 (and_1_out, d_flipflop_asc_1_q, mir_1_jam[1]);
  D_FlipFlop_Asc d_flipflop_asc_1 (
    .D(N), .CLK(CLK), .Q(d_flipflop_asc_1_q), .nPRE(1'b1), .nCLR(not_1_out));  // open: nQ
  D_FlipFlop_Asc d_flipflop_asc_2 (
    .D(Z), .CLK(CLK), .Q(d_flipflop_asc_2_q), .nPRE(1'b1), .nCLR(not_1_out));  // open: nQ
  Multiplexer #(.width(8), .enable("false")) multiplexer_3 (
    .in0(mir_1_addr), .in1(or_2_out), .out(multiplexer_3_out), .sel(mir_1_jam[2]));
  or or_1 (or_1_out[8], and_1_out, and_2_out, mir_1_addr_2[8]);
  and and_2 (and_2_out, d_flipflop_asc_2_q, mir_1_jam[0]);
  assign or_2_out = MBR | mir_1_addr;  // OR_Gate or_2, 8 bits wide
  not not_1 (not_1_out, RESET);
  MPC mpc_1 (
    .Entrada({or_1_out[8], multiplexer_3_out}), .CLK(CLK), .Salida(MPC), .nPRE(multiplexer_1_out),
    .nCLR(multiplexer_2_out));
  Control_Store control_store_1 (.CS_E(MPC), .CS_S32(control_store_1_cs_s32), .CS_S4(control_store_1_cs_s4));
  MIR mir_1 (
    .Entrada_4(control_store_1_cs_s4), .Entrada_32(control_store_1_cs_s32), .CLK(CLK), .RESET(RESET),
    .B(mir_1_b), .Mem(Mem), .C({H_C, OPC_C, TOS_C, CPP_C, LV_C, SP_C, PC_C, MDR_C, MAR_C}),
    .ALU({Shifter, ALU}), .JAM(mir_1_jam), .Addr({mir_1_addr_2[8], mir_1_addr}));
  Decoder #(.select(4), .enable("false")) decoder_1 (
    .out0(MDR_B), .out1(PC_B), .out2(MBR_B), .out3(MBRU_B), .out4(SP_B), .out5(LV_B), .out6(CPP_B),
    .out7(TOS_B), .out8(OPC_B), .sel(mir_1_b));  // open: out9, out10, out11, out12, out13, out14, out15
endmodule

module Control_Store (
  input  [8:0] CS_E,
  output [31:0] CS_S32,
  output [3:0] CS_S4
);

  ROM #(.addrWidth(9), .dataWidth(32)) rom_1 (.addr(CS_E), .data(CS_S32), .sel(1'b1));
  ROM #(.addrWidth(9), .dataWidth(4)) rom_2 (.addr(CS_E), .data(CS_S4), .sel(1'b1));

  // Notes on the sheet:
  //   Otra truchada porque Logisim no tiene
  //   un bloque de memoria mas ancho que 32 bits
  //   contents of rom_1 (hex, n*v repeats v):
  //   80000000 255*0 435021
  //   contents of rom_2 (hex, n*v repeats v):
  //   f 255*0 1
endmodule

module MPC (
  input  [8:0] nPRE,
  input  [8:0] Entrada,
  input  CLK,
  input  [8:0] nCLR,
  output [8:0] Salida
);

  D_Latch d_latch_1 (.D(Entrada[8]), .CLK(CLK), .Q(Salida[8]), .nPRE(nPRE[8]), .nCLR(nCLR[8]));  // open: nQ
  D_Latch d_latch_2 (.D(Entrada[7]), .CLK(CLK), .Q(Salida[7]), .nPRE(nPRE[7]), .nCLR(nCLR[7]));  // open: nQ
  D_Latch d_latch_3 (.D(Entrada[6]), .CLK(CLK), .Q(Salida[6]), .nPRE(nPRE[6]), .nCLR(nCLR[6]));  // open: nQ
  D_Latch d_latch_4 (.D(Entrada[5]), .CLK(CLK), .Q(Salida[5]), .nPRE(nPRE[5]), .nCLR(nCLR[5]));  // open: nQ
  D_Latch d_latch_5 (.D(Entrada[4]), .CLK(CLK), .Q(Salida[4]), .nPRE(nPRE[4]), .nCLR(nCLR[4]));  // open: nQ
  D_Latch d_latch_6 (.D(Entrada[3]), .CLK(CLK), .Q(Salida[3]), .nPRE(nPRE[3]), .nCLR(nCLR[3]));  // open: nQ
  D_Latch d_latch_7 (.D(Entrada[2]), .CLK(CLK), .Q(Salida[2]), .nPRE(nPRE[2]), .nCLR(nCLR[2]));  // open: nQ
  D_Latch d_latch_8 (.D(Entrada[1]), .CLK(CLK), .Q(Salida[1]), .nPRE(nPRE[1]), .nCLR(nCLR[1]));  // open: nQ
  D_Latch d_latch_9 (.D(Entrada[0]), .CLK(CLK), .Q(Salida[0]), .nPRE(nPRE[0]), .nCLR(nCLR[0]));  // open: nQ
endmodule

module MIR (
  input  [3:0] Entrada_4,
  input  [31:0] Entrada_32,
  input  CLK,
  input  RESET,
  output [3:0] B,
  output [2:0] Mem,
  output [8:0] C,
  output [7:0] ALU,
  output [2:0] JAM,
  output [8:0] Addr
);

  wire [3:0] multiplexer_2_out, multiplexer_4_out, not_2_out;
  wire [31:0] multiplexer_1_out, multiplexer_3_out, not_1_out;

  Multiplexer #(.width(32), .enable("false")) multiplexer_1 (
    .in0({32{1'b1}}), .in1(not_1_out), .out(multiplexer_1_out), .sel(RESET));
  assign not_1_out = ~32'h435021;  // NOT_Gate not_1, 32 bits wide
  assign not_2_out = ~4'b0001;  // NOT_Gate not_2, 4 bits wide
  Multiplexer #(.width(4), .enable("false")) multiplexer_2 (
    .in0(4'b1111), .in1(not_2_out), .out(multiplexer_2_out), .sel(RESET));
  Multiplexer #(.width(32), .enable("false")) multiplexer_3 (
    .in0({32{1'b1}}), .in1(32'h435021), .out(multiplexer_3_out), .sel(RESET));
  Multiplexer #(.width(4), .enable("false")) multiplexer_4 (
    .in0(4'b1111), .in1(4'b0001), .out(multiplexer_4_out), .sel(RESET));
  Register_32_bits_Des register_32_bits_des_1 (
    .Entrada(Entrada_32), .CLK(CLK), .Salida({Addr, JAM, ALU, C, Mem}), .nPRE(multiplexer_1_out),
    .nCLR(multiplexer_3_out));
  Register_4_bits_Des register_4_bits_des_1 (
    .Entrada(Entrada_4), .CLK(CLK), .Salida(B), .nPRE(multiplexer_2_out), .nCLR(multiplexer_4_out));
endmodule

module Data_Path (
  input  MAR_C,
  input  [31:0] MEM_RD,
  input  MDR_B,
  input  MDR_C,
  input  rd,
  input  [7:0] MEM_FETCH,
  input  PC_B,
  input  PC_C,
  input  MBR,
  input  fetch,
  input  MBRU,
  input  SP_B,
  input  SP_C,
  input  LV_B,
  input  LV_C,
  input  CPP_B,
  input  CPP_C,
  input  RESET,
  input  TOS_B,
  input  TOS_C,
  input  OPC_B,
  input  OPC_C,
  input  H_C,
  input  INVA,
  input  ENA,
  input  CLK,
  input  ENB,
  input  INC,
  input  [1:0] F,
  input  SRA1,
  input  SLL8,
  output [31:0] MEM_MAR,
  output [31:0] MEM_WR,
  output [31:0] MEM_PC,
  output [7:0] OP_CODE,
  output [31:0] B,
  output N,
  output Z,
  output [31:0] C
);

  wire [7:0] multiplexer_1_out;
  wire [31:0] multiplexer_2_out, multiplexer_3_out, register_32_bits_hold_paralel_load_4_salida,
       register_32_bits_hold_paralel_load_5_salida, register_32_bits_hold_paralel_load_6_salida,
       register_32_bits_hold_paralel_load_7_salida, register_32_bits_hold_paralel_load_8_salida;

  Multiplexer #(.width(8), .enable("false")) multiplexer_1 (
    .in0({8{1'b1}}), .in1({8{1'b0}}), .out(multiplexer_1_out), .sel(RESET));
  Multiplexer #(.width(32), .enable("false")) multiplexer_2 (
    .in0({32{1'b1}}), .in1({32{1'b0}}), .out(multiplexer_2_out), .sel(RESET));
  Multiplexer #(.width(32), .enable("false")) multiplexer_3 (.in0(C), .in1(MEM_RD), .out(multiplexer_3_out), .sel(rd));
  Register_8_bits_Hold___Paralel_Load register_8_bits_hold_paralel_load_1 (
    .Entrada(MEM_FETCH), .LOAD(fetch), .CLK(CLK), .Salida(OP_CODE), .nPRE({8{1'b1}}), .nCLR(multiplexer_1_out));
  Register_32_bits_Hold___Paralel_Load register_32_bits_hold_paralel_load_1 (
    .Entrada(C), .LOAD(MAR_C), .nPRE({32{1'b1}}), .CLK(CLK), .Salida(MEM_MAR), .nCLR(multiplexer_2_out));
  assign B = MDR_B ? MEM_WR : 32'bz;  // Controlled_Buffer controlled_buffer_1
  Register_32_bits_Hold___Paralel_Load register_32_bits_hold_paralel_load_2 (
    .Entrada(multiplexer_3_out), .LOAD(MDR_C), .nPRE({32{1'b1}}), .CLK(CLK), .Salida(MEM_WR),
    .nCLR(multiplexer_2_out));
  Register_32_bits_Hold___Paralel_Load register_32_bits_hold_paralel_load_3 (
    .Entrada(C), .LOAD(PC_C), .nPRE({32{1'b1}}), .CLK(CLK), .Salida(MEM_PC), .nCLR(multiplexer_2_out));
  assign B = PC_B ? MEM_PC : 32'bz;  // Controlled_Buffer controlled_buffer_2
  MBR_EN mbr_en_1 (.in_1(OP_CODE), .Salida_Signada(B), .Salida_No_Signada(B), .MRB(MBR), .MBRU(MBRU));
  Register_32_bits_Hold___Paralel_Load register_32_bits_hold_paralel_load_4 (
    .Entrada(C), .LOAD(SP_C), .nPRE({32{1'b1}}), .CLK(CLK),
    .Salida(register_32_bits_hold_paralel_load_4_salida), .nCLR(multiplexer_2_out));
  assign B = SP_B ? register_32_bits_hold_paralel_load_4_salida : 32'bz;  // Controlled_Buffer controlled_buffer_3
  Register_32_bits_Hold___Paralel_Load register_32_bits_hold_paralel_load_5 (
    .Entrada(C), .LOAD(LV_C), .nPRE({32{1'b1}}), .CLK(CLK),
    .Salida(register_32_bits_hold_paralel_load_5_salida), .nCLR(multiplexer_2_out));
  assign B = LV_B ? register_32_bits_hold_paralel_load_5_salida : 32'bz;  // Controlled_Buffer controlled_buffer_4
  assign B = CPP_B ? register_32_bits_hold_paralel_load_6_salida : 32'bz;  // Controlled_Buffer controlled_buffer_5
  Register_32_bits_Hold___Paralel_Load register_32_bits_hold_paralel_load_6 (
    .Entrada(C), .LOAD(CPP_C), .nPRE({32{1'b1}}), .CLK(CLK),
    .Salida(register_32_bits_hold_paralel_load_6_salida), .nCLR(multiplexer_2_out));
  assign B = TOS_B ? register_32_bits_hold_paralel_load_7_salida : 32'bz;  // Controlled_Buffer controlled_buffer_6
  Register_32_bits_Hold___Paralel_Load register_32_bits_hold_paralel_load_7 (
    .Entrada(C), .LOAD(TOS_C), .nPRE({32{1'b1}}), .CLK(CLK),
    .Salida(register_32_bits_hold_paralel_load_7_salida), .nCLR(multiplexer_2_out));
  Register_32_bits_Hold___Paralel_Load register_32_bits_hold_paralel_load_8 (
    .Entrada(C), .LOAD(OPC_C), .nPRE({32{1'b1}}), .CLK(CLK),
    .Salida(register_32_bits_hold_paralel_load_8_salida), .nCLR(multiplexer_2_out));
  assign B = OPC_B ? register_32_bits_hold_paralel_load_8_salida : 32'bz;  // Controlled_Buffer controlled_buffer_7
  Register_32_bits_Hold___Paralel_Load register_32_bits_hold_paralel_load_9 (
    .Entrada(C), .LOAD(H_C), .nPRE({32{1'b1}}), .CLK(CLK), .nCLR(multiplexer_2_out));  // open: Salida
  Desplazador desplazador_1 (.SRA1(SRA1), .SLL8(SLL8), .Salida(C));  // open: Entrada
  ALU_1_bit alu_1_bit_1 (.INVA(INVA), .ENA(ENA), .ENB(ENB), .F(F), .Cin(INC));  // open: A, B, Salida, Cout

  // Notes on the sheet:
  //   Preset 8 Bits
  //   Clear 8 Bits
  //   Preset 32 Bits
  //   Clear 32 Bits
  //   Bus B
  //   Bus C
endmodule

module Register_32_bits_Hold___Paralel_Load (
  input  [31:0] nPRE,
  input  [31:0] Entrada,
  input  LOAD,
  input  CLK,
  input  [31:0] nCLR,
  output [31:0] Salida
);

  wire [31:0] multiplexer_1_out;

  Multiplexer #(.width(32), .enable("false")) multiplexer_1 (
    .in1(Entrada), .out(multiplexer_1_out), .sel(LOAD));  // open: in0
  D_FlipFlop_Des d_flipflop_des_1 (
    .D(multiplexer_1_out[31]), .CLK(CLK), .Q(Salida[31]), .nPRE(nPRE[31]), .nCLR(nCLR[31]));  // open: nQ
  D_FlipFlop_Des d_flipflop_des_2 (
    .D(multiplexer_1_out[30]), .CLK(CLK), .Q(Salida[30]), .nPRE(nPRE[30]), .nCLR(nCLR[30]));  // open: nQ
  D_FlipFlop_Des d_flipflop_des_3 (
    .D(multiplexer_1_out[29]), .CLK(CLK), .Q(Salida[29]), .nPRE(nPRE[29]), .nCLR(nCLR[29]));  // open: nQ
  D_FlipFlop_Des d_flipflop_des_4 (
    .D(multiplexer_1_out[28]), .CLK(CLK), .Q(Salida[28]), .nPRE(nPRE[28]), .nCLR(nCLR[28]));  // open: nQ
  D_FlipFlop_Des d_flipflop_des_5 (
    .D(multiplexer_1_out[27]), .CLK(CLK), .Q(Salida[27]), .nPRE(nPRE[27]), .nCLR(nCLR[27]));  // open: nQ
  D_FlipFlop_Des d_flipflop_des_6 (
    .D(multiplexer_1_out[26]), .CLK(CLK), .Q(Salida[26]), .nPRE(nPRE[26]), .nCLR(nCLR[26]));  // open: nQ
  D_FlipFlop_Des d_flipflop_des_7 (
    .D(multiplexer_1_out[25]), .CLK(CLK), .Q(Salida[25]), .nPRE(nPRE[25]), .nCLR(nCLR[25]));  // open: nQ
  D_FlipFlop_Des d_flipflop_des_8 (
    .D(multiplexer_1_out[24]), .CLK(CLK), .Q(Salida[24]), .nPRE(nPRE[24]), .nCLR(nCLR[24]));  // open: nQ
  D_FlipFlop_Des d_flipflop_des_9 (
    .D(multiplexer_1_out[23]), .CLK(CLK), .Q(Salida[23]), .nPRE(nPRE[23]), .nCLR(nCLR[23]));  // open: nQ
  D_FlipFlop_Des d_flipflop_des_10 (
    .D(multiplexer_1_out[22]), .CLK(CLK), .Q(Salida[22]), .nPRE(nPRE[22]), .nCLR(nCLR[22]));  // open: nQ
  D_FlipFlop_Des d_flipflop_des_11 (
    .D(multiplexer_1_out[21]), .CLK(CLK), .Q(Salida[21]), .nPRE(nPRE[21]), .nCLR(nCLR[21]));  // open: nQ
  D_FlipFlop_Des d_flipflop_des_12 (
    .D(multiplexer_1_out[20]), .CLK(CLK), .Q(Salida[20]), .nPRE(nPRE[20]), .nCLR(nCLR[20]));  // open: nQ
  D_FlipFlop_Des d_flipflop_des_13 (
    .D(multiplexer_1_out[19]), .CLK(CLK), .Q(Salida[19]), .nPRE(nPRE[19]), .nCLR(nCLR[19]));  // open: nQ
  D_FlipFlop_Des d_flipflop_des_14 (
    .D(multiplexer_1_out[18]), .CLK(CLK), .Q(Salida[18]), .nPRE(nPRE[18]), .nCLR(nCLR[18]));  // open: nQ
  D_FlipFlop_Des d_flipflop_des_15 (
    .D(multiplexer_1_out[17]), .CLK(CLK), .Q(Salida[17]), .nPRE(nPRE[17]), .nCLR(nCLR[17]));  // open: nQ
  D_FlipFlop_Des d_flipflop_des_16 (
    .D(multiplexer_1_out[16]), .CLK(CLK), .Q(Salida[16]), .nPRE(nPRE[16]), .nCLR(nCLR[16]));  // open: nQ
  D_FlipFlop_Des d_flipflop_des_17 (
    .D(multiplexer_1_out[15]), .CLK(CLK), .Q(Salida[15]), .nPRE(nPRE[15]), .nCLR(nCLR[15]));  // open: nQ
  D_FlipFlop_Des d_flipflop_des_18 (
    .D(multiplexer_1_out[14]), .CLK(CLK), .Q(Salida[14]), .nPRE(nPRE[14]), .nCLR(nCLR[14]));  // open: nQ
  D_FlipFlop_Des d_flipflop_des_19 (
    .D(multiplexer_1_out[13]), .CLK(CLK), .Q(Salida[13]), .nPRE(nPRE[13]), .nCLR(nCLR[13]));  // open: nQ
  D_FlipFlop_Des d_flipflop_des_20 (
    .D(multiplexer_1_out[12]), .CLK(CLK), .Q(Salida[12]), .nPRE(nPRE[12]), .nCLR(nCLR[12]));  // open: nQ
  D_FlipFlop_Des d_flipflop_des_21 (
    .D(multiplexer_1_out[11]), .CLK(CLK), .Q(Salida[11]), .nPRE(nPRE[11]), .nCLR(nCLR[11]));  // open: nQ
  D_FlipFlop_Des d_flipflop_des_22 (
    .D(multiplexer_1_out[10]), .CLK(CLK), .Q(Salida[10]), .nPRE(nPRE[10]), .nCLR(nCLR[10]));  // open: nQ
  D_FlipFlop_Des d_flipflop_des_23 (
    .D(multiplexer_1_out[9]), .CLK(CLK), .Q(Salida[9]), .nPRE(nPRE[9]), .nCLR(nCLR[9]));  // open: nQ
  D_FlipFlop_Des d_flipflop_des_24 (
    .D(multiplexer_1_out[8]), .CLK(CLK), .Q(Salida[8]), .nPRE(nPRE[8]), .nCLR(nCLR[8]));  // open: nQ
  D_FlipFlop_Des d_flipflop_des_25 (
    .D(multiplexer_1_out[7]), .CLK(CLK), .Q(Salida[7]), .nPRE(nPRE[7]), .nCLR(nCLR[7]));  // open: nQ
  D_FlipFlop_Des d_flipflop_des_26 (
    .D(multiplexer_1_out[6]), .CLK(CLK), .Q(Salida[6]), .nPRE(nPRE[6]), .nCLR(nCLR[6]));  // open: nQ
  D_FlipFlop_Des d_flipflop_des_27 (
    .D(multiplexer_1_out[5]), .CLK(CLK), .Q(Salida[5]), .nPRE(nPRE[5]), .nCLR(nCLR[5]));  // open: nQ
  D_FlipFlop_Des d_flipflop_des_28 (
    .D(multiplexer_1_out[4]), .CLK(CLK), .Q(Salida[4]), .nPRE(nPRE[4]), .nCLR(nCLR[4]));  // open: nQ
  D_FlipFlop_Des d_flipflop_des_29 (
    .D(multiplexer_1_out[3]), .CLK(CLK), .Q(Salida[3]), .nPRE(nPRE[3]), .nCLR(nCLR[3]));  // open: nQ
  D_FlipFlop_Des d_flipflop_des_30 (
    .D(multiplexer_1_out[2]), .CLK(CLK), .Q(Salida[2]), .nPRE(nPRE[2]), .nCLR(nCLR[2]));  // open: nQ
  D_FlipFlop_Des d_flipflop_des_31 (
    .D(multiplexer_1_out[1]), .CLK(CLK), .Q(Salida[1]), .nPRE(nPRE[1]), .nCLR(nCLR[1]));  // open: nQ
  D_FlipFlop_Des d_flipflop_des_32 (
    .D(multiplexer_1_out[0]), .CLK(CLK), .Q(Salida[0]), .nPRE(nPRE[0]), .nCLR(nCLR[0]));  // open: nQ
endmodule

module Register_32_bits_Des (
  input  [31:0] nPRE,
  input  [31:0] Entrada,
  input  CLK,
  input  [31:0] nCLR,
  output [31:0] Salida
);

  D_FlipFlop_Des d_flipflop_des_1 (
    .D(Entrada[31]), .CLK(CLK), .Q(Salida[31]), .nPRE(nPRE[31]), .nCLR(nCLR[31]));  // open: nQ
  D_FlipFlop_Des d_flipflop_des_2 (
    .D(Entrada[30]), .CLK(CLK), .Q(Salida[30]), .nPRE(nPRE[30]), .nCLR(nCLR[30]));  // open: nQ
  D_FlipFlop_Des d_flipflop_des_3 (
    .D(Entrada[29]), .CLK(CLK), .Q(Salida[29]), .nPRE(nPRE[29]), .nCLR(nCLR[29]));  // open: nQ
  D_FlipFlop_Des d_flipflop_des_4 (
    .D(Entrada[28]), .CLK(CLK), .Q(Salida[28]), .nPRE(nPRE[28]), .nCLR(nCLR[28]));  // open: nQ
  D_FlipFlop_Des d_flipflop_des_5 (
    .D(Entrada[27]), .CLK(CLK), .Q(Salida[27]), .nPRE(nPRE[27]), .nCLR(nCLR[27]));  // open: nQ
  D_FlipFlop_Des d_flipflop_des_6 (
    .D(Entrada[26]), .CLK(CLK), .Q(Salida[26]), .nPRE(nPRE[26]), .nCLR(nCLR[26]));  // open: nQ
  D_FlipFlop_Des d_flipflop_des_7 (
    .D(Entrada[25]), .CLK(CLK), .Q(Salida[25]), .nPRE(nPRE[25]), .nCLR(nCLR[25]));  // open: nQ
  D_FlipFlop_Des d_flipflop_des_8 (
    .D(Entrada[24]), .CLK(CLK), .Q(Salida[24]), .nPRE(nPRE[24]), .nCLR(nCLR[24]));  // open: nQ
  D_FlipFlop_Des d_flipflop_des_9 (
    .D(Entrada[23]), .CLK(CLK), .Q(Salida[23]), .nPRE(nPRE[23]), .nCLR(nCLR[23]));  // open: nQ
  D_FlipFlop_Des d_flipflop_des_10 (
    .D(Entrada[22]), .CLK(CLK), .Q(Salida[22]), .nPRE(nPRE[22]), .nCLR(nCLR[22]));  // open: nQ
  D_FlipFlop_Des d_flipflop_des_11 (
    .D(Entrada[21]), .CLK(CLK), .Q(Salida[21]), .nPRE(nPRE[21]), .nCLR(nCLR[21]));  // open: nQ
  D_FlipFlop_Des d_flipflop_des_12 (
    .D(Entrada[20]), .CLK(CLK), .Q(Salida[20]), .nPRE(nPRE[20]), .nCLR(nCLR[20]));  // open: nQ
  D_FlipFlop_Des d_flipflop_des_13 (
    .D(Entrada[19]), .CLK(CLK), .Q(Salida[19]), .nPRE(nPRE[19]), .nCLR(nCLR[19]));  // open: nQ
  D_FlipFlop_Des d_flipflop_des_14 (
    .D(Entrada[18]), .CLK(CLK), .Q(Salida[18]), .nPRE(nPRE[18]), .nCLR(nCLR[18]));  // open: nQ
  D_FlipFlop_Des d_flipflop_des_15 (
    .D(Entrada[17]), .CLK(CLK), .Q(Salida[17]), .nPRE(nPRE[17]), .nCLR(nCLR[17]));  // open: nQ
  D_FlipFlop_Des d_flipflop_des_16 (
    .D(Entrada[16]), .CLK(CLK), .Q(Salida[16]), .nPRE(nPRE[16]), .nCLR(nCLR[16]));  // open: nQ
  D_FlipFlop_Des d_flipflop_des_17 (
    .D(Entrada[15]), .CLK(CLK), .Q(Salida[15]), .nPRE(nPRE[15]), .nCLR(nCLR[15]));  // open: nQ
  D_FlipFlop_Des d_flipflop_des_18 (
    .D(Entrada[14]), .CLK(CLK), .Q(Salida[14]), .nPRE(nPRE[14]), .nCLR(nCLR[14]));  // open: nQ
  D_FlipFlop_Des d_flipflop_des_19 (
    .D(Entrada[13]), .CLK(CLK), .Q(Salida[13]), .nPRE(nPRE[13]), .nCLR(nCLR[13]));  // open: nQ
  D_FlipFlop_Des d_flipflop_des_20 (
    .D(Entrada[12]), .CLK(CLK), .Q(Salida[12]), .nPRE(nPRE[12]), .nCLR(nCLR[12]));  // open: nQ
  D_FlipFlop_Des d_flipflop_des_21 (
    .D(Entrada[11]), .CLK(CLK), .Q(Salida[11]), .nPRE(nPRE[11]), .nCLR(nCLR[11]));  // open: nQ
  D_FlipFlop_Des d_flipflop_des_22 (
    .D(Entrada[10]), .CLK(CLK), .Q(Salida[10]), .nPRE(nPRE[10]), .nCLR(nCLR[10]));  // open: nQ
  D_FlipFlop_Des d_flipflop_des_23 (
    .D(Entrada[9]), .CLK(CLK), .Q(Salida[9]), .nPRE(nPRE[9]), .nCLR(nCLR[9]));  // open: nQ
  D_FlipFlop_Des d_flipflop_des_24 (
    .D(Entrada[8]), .CLK(CLK), .Q(Salida[8]), .nPRE(nPRE[8]), .nCLR(nCLR[8]));  // open: nQ
  D_FlipFlop_Des d_flipflop_des_25 (
    .D(Entrada[7]), .CLK(CLK), .Q(Salida[7]), .nPRE(nPRE[7]), .nCLR(nCLR[7]));  // open: nQ
  D_FlipFlop_Des d_flipflop_des_26 (
    .D(Entrada[6]), .CLK(CLK), .Q(Salida[6]), .nPRE(nPRE[6]), .nCLR(nCLR[6]));  // open: nQ
  D_FlipFlop_Des d_flipflop_des_27 (
    .D(Entrada[5]), .CLK(CLK), .Q(Salida[5]), .nPRE(nPRE[5]), .nCLR(nCLR[5]));  // open: nQ
  D_FlipFlop_Des d_flipflop_des_28 (
    .D(Entrada[4]), .CLK(CLK), .Q(Salida[4]), .nPRE(nPRE[4]), .nCLR(nCLR[4]));  // open: nQ
  D_FlipFlop_Des d_flipflop_des_29 (
    .D(Entrada[3]), .CLK(CLK), .Q(Salida[3]), .nPRE(nPRE[3]), .nCLR(nCLR[3]));  // open: nQ
  D_FlipFlop_Des d_flipflop_des_30 (
    .D(Entrada[2]), .CLK(CLK), .Q(Salida[2]), .nPRE(nPRE[2]), .nCLR(nCLR[2]));  // open: nQ
  D_FlipFlop_Des d_flipflop_des_31 (
    .D(Entrada[1]), .CLK(CLK), .Q(Salida[1]), .nPRE(nPRE[1]), .nCLR(nCLR[1]));  // open: nQ
  D_FlipFlop_Des d_flipflop_des_32 (
    .D(Entrada[0]), .CLK(CLK), .Q(Salida[0]), .nPRE(nPRE[0]), .nCLR(nCLR[0]));  // open: nQ
endmodule

module Register_8_bits_Hold___Paralel_Load (
  input  [7:0] nPRE,
  input  [7:0] Entrada,
  input  [7:0] nCLR,
  input  LOAD,
  input  CLK,
  output [7:0] Salida
);

  Multiplexer #(.width(8), .enable("false")) multiplexer_1 (.in1(Entrada), .sel(LOAD));  // open: in0, out
endmodule

module Register_4_bits_Des (
  input  [3:0] nPRE,
  input  [3:0] Entrada,
  input  CLK,
  input  [3:0] nCLR,
  output [3:0] Salida
);

  D_FlipFlop_Des d_flipflop_des_1 (
    .D(Entrada[3]), .CLK(CLK), .Q(Salida[3]), .nPRE(nPRE[3]), .nCLR(nCLR[3]));  // open: nQ
  D_FlipFlop_Des d_flipflop_des_2 (
    .D(Entrada[2]), .CLK(CLK), .Q(Salida[2]), .nPRE(nPRE[2]), .nCLR(nCLR[2]));  // open: nQ
  D_FlipFlop_Des d_flipflop_des_3 (
    .D(Entrada[1]), .CLK(CLK), .Q(Salida[1]), .nPRE(nPRE[1]), .nCLR(nCLR[1]));  // open: nQ
  D_FlipFlop_Des d_flipflop_des_4 (
    .D(Entrada[0]), .CLK(CLK), .Q(Salida[0]), .nPRE(nPRE[0]), .nCLR(nCLR[0]));  // open: nQ
endmodule

module MBR_EN (
  input  [7:0] in_1,
  input  MRB,
  input  MBRU,
  output [31:0] Salida_Signada,
  output [31:0] Salida_No_Signada
);

  assign Salida_Signada = MRB ? {{25{in_1[7]}}, in_1[6:0]} : 32'bz;  // Controlled_Buffer controlled_buffer_1
  assign Salida_No_Signada = MBRU ? {{24{1'b0}}, in_1} : 32'bz;  // Controlled_Buffer controlled_buffer_2
endmodule

module D_FlipFlop_Des (
  input  nPRE,
  input  D,
  input  CLK,
  input  nCLR,
  output Q,
  output nQ
);

  wire d_latch_1_q, not_1_out;

  D_Latch d_latch_1 (.D(D), .CLK(CLK), .Q(d_latch_1_q), .nPRE(nPRE), .nCLR(nCLR));  // open: nQ
  not not_1 (not_1_out, CLK);
  D_Latch d_latch_2 (.D(d_latch_1_q), .CLK(not_1_out), .Q(Q), .nQ(nQ), .nPRE(nPRE), .nCLR(nCLR));
endmodule

module D_FlipFlop_Asc (
  input  nPRE,
  input  D,
  input  CLK,
  input  nCLR,
  output Q,
  output nQ
);
endmodule

module D_Latch (
  input  nPRE,
  input  D,
  input  CLK,
  input  nCLR,
  output Q,
  output nQ
);
endmodule

module ALU_1_bit (
  input  Cin,
  input  INVA,
  input  A,
  input  ENA,
  input  B,
  input  ENB,
  input  [1:0] F,
  output Salida,
  output Cout
);
endmodule

module Unidad_Logica__ALU (
  input  A,
  input  B,
  input  EN1,
  input  EN2,
  input  EN3,
  output AND,
  output OR,
  output NOT
);
endmodule

module Sumador_Completo__ALU (
  input  Cin,
  input  A,
  input  B,
  input  EN,
  output S,
  output Cout
);
endmodule

module Desplazador (
  input  [31:0] Entrada,
  input  SRA1,
  input  SLL8,
  output [31:0] Salida
);
endmodule
