// Logisim project MIC-1Mejorado.circ as structural Verilog: 25 circuits, main circuit main
module main (
  input  CLK,
  output [31:0] PC,
  output [8:0] MPC,
  output [31:0] B,
  output [31:0] C
);

  wire control_unit_1_cpp_b, control_unit_1_cpp_c, control_unit_1_h_c, control_unit_1_lv_b,
       control_unit_1_lv_c, control_unit_1_mar_c, control_unit_1_mbr_b, control_unit_1_mbru_b,
       control_unit_1_mdr_b, control_unit_1_mdr_c, control_unit_1_opc_b, control_unit_1_opc_c,
       control_unit_1_pc_b, control_unit_1_pc_c, control_unit_1_sp_b, control_unit_1_sp_c,
       control_unit_1_tos_b, control_unit_1_tos_c, data_path_1_n, data_path_1_z, RESET_out;
  wire [1:0] control_unit_1_alu_2, control_unit_1_shifter;
  wire [2:0] control_unit_1_mem;
  wire [3:0] control_unit_1_alu;
  wire [7:0] mem_1_mem_fetch, undriven;
  wire [31:0] data_path_1_mem_mar, data_path_1_mem_wr, mem_1_mrm_rd;

  Mem mem_1 (
    .MEM_ADDR_32(data_path_1_mem_mar), .CLK(CLK), .MEM_WR(data_path_1_mem_wr), .MRM_RD(mem_1_mrm_rd),
    .MEM_FETCH(mem_1_mem_fetch), .wr(control_unit_1_mem[2]), .rd(control_unit_1_mem[1]),
    .fetch(control_unit_1_mem[0]), .MEM_ADDR_8(PC));
  Button RESET (.out(RESET_out));
  Data_Path data_path_1 (
    .MEM_WR(data_path_1_mem_wr), .MEM_RD(mem_1_mrm_rd), .rd(control_unit_1_mem[1]),
    .MEM_FETCH(mem_1_mem_fetch), .RESET(RESET_out), .INVA(control_unit_1_alu[1]),
    .ENA(control_unit_1_alu[3]), .CLK(CLK), .ENB(control_unit_1_alu[2]), .INC(control_unit_1_alu[0]),
    .F(control_unit_1_alu_2), .SRA1(control_unit_1_shifter[0]), .SLL8(control_unit_1_shifter[1]),
    .MEM_MAR(data_path_1_mem_mar), .N(data_path_1_n), .Z(data_path_1_z), .MAR_C(control_unit_1_mar_c),
    .MDR_C(control_unit_1_mdr_c), .PC_C(control_unit_1_pc_c), .fetch(control_unit_1_mem[0]),
    .SP_C(control_unit_1_sp_c), .LV_C(control_unit_1_lv_c), .CPP_C(control_unit_1_cpp_c),
    .TOS_C(control_unit_1_tos_c), .OPC_C(control_unit_1_opc_c), .H_C(control_unit_1_h_c),
    .MBR(control_unit_1_mbr_b), .MBRU(control_unit_1_mbru_b), .MDR_B(control_unit_1_mdr_b),
    .PC_B(control_unit_1_pc_b), .SP_B(control_unit_1_sp_b), .LV_B(control_unit_1_lv_b),
    .CPP_B(control_unit_1_cpp_b), .TOS_B(control_unit_1_tos_b), .OPC_B(control_unit_1_opc_b), .MEM_PC(PC),
    .B(B), .C(C));  // open: OP_CODE
  Control_Unit control_unit_1 (
    .CLK(CLK), .RESET(RESET_out), .MBR(undriven), .N(data_path_1_n), .Z(data_path_1_z), .MPC(MPC),
    .MDR_B(control_unit_1_mdr_b), .PC_B(control_unit_1_pc_b), .MBR_B(control_unit_1_mbr_b),
    .MBRU_B(control_unit_1_mbru_b), .SP_B(control_unit_1_sp_b), .LV_B(control_unit_1_lv_b),
    .CPP_B(control_unit_1_cpp_b), .TOS_B(control_unit_1_tos_b), .OPC_B(control_unit_1_opc_b),
    .Mem(control_unit_1_mem), .ALU({control_unit_1_alu_2, control_unit_1_alu}),
    .Shifter(control_unit_1_shifter), .H_C(control_unit_1_h_c), .OPC_C(control_unit_1_opc_c),
    .TOS_C(control_unit_1_tos_c), .CPP_C(control_unit_1_cpp_c), .LV_C(control_unit_1_lv_c),
    .SP_C(control_unit_1_sp_c), .PC_C(control_unit_1_pc_c), .MDR_C(control_unit_1_mdr_c),
    .MAR_C(control_unit_1_mar_c));
endmodule

module Mem (
  input  wr,
  input  [31:0] MEM_WR,
  input  [31:0] MEM_ADDR_32,
  input  rd,
  input  [31:0] MEM_ADDR_8,
  input  fetch,
  input  CLK,
  output [31:0] MRM_RD,
  output [7:0] MEM_FETCH
);

  wire not_1_out, not_2_out, not_3_out;
  wire [7:0] ram_2_data;
  wire [31:0] ram_1_data;

  not not_1 (not_1_out, CLK);
  not not_2 (not_2_out, wr);
  RAM #(.addrWidth(24), .dataWidth(32)) ram_1 (
    .addr(MEM_ADDR_32[23:0]), .data(ram_1_data), .sel(1'b1), .clk(not_1_out), .ld(not_2_out), .clr(1'b0));
  assign ram_1_data = wr ? MEM_WR : 32'bz;  // Controlled_Buffer controlled_buffer_1
  assign MRM_RD = rd ? ram_1_data : 32'bz;  // Controlled_Buffer controlled_buffer_2
  not not_3 (not_3_out, CLK);
  RAM #(.addrWidth(24)) ram_2 (
    .addr(MEM_ADDR_8[23:0]), .data(ram_2_data), .sel(1'b1), .clk(not_3_out), .clr(1'b0));  // open: ld
  assign MEM_FETCH = fetch ? ram_2_data : 8'bz;  // Controlled_Buffer controlled_buffer_3

  // Notes on the sheet:
  //   Una truchada porque Logisim no tiene
  //   un bloque de memoria con dos canales de datos
endmodule

module Control_Unit (
  input  CLK,
  input  RESET,
  input  [7:0] MBR,
  input  N,
  input  Z,
  output [8:0] MPC,
  output MDR_B,
  output PC_B,
  output MBR_B,
  output MBRU_B,
  output SP_B,
  output LV_B,
  output CPP_B,
  output TOS_B,
  output OPC_B,
  output [2:0] Mem,
  output [5:0] ALU,
  output [1:0] Shifter,
  output H_C,
  output OPC_C,
  output TOS_C,
  output CPP_C,
  output LV_C,
  output SP_C,
  output PC_C,
  output MDR_C,
  output MAR_C
);

  wire and_1_out, and_2_out, d_flipflop_asc_1_q, d_flipflop_asc_2_q, not_1_out;
  wire [2:0] mir_1_jam;
  wire [3:0] control_store_1_cs_s4, mir_1_b;
  wire [7:0] mir_1_addr, multiplexer_3_out, or_2_out;
  wire [8:0] multiplexer_1_out, multiplexer_2_out;
  wire [8:8] mir_1_addr_2, or_1_out;
  wire [31:0] control_store_1_cs_s32;

  Multiplexer #(.width(9), .enable("false")) multiplexer_1 (
    .in0({9{1'b1}}), .in1(9'hff), .out(multiplexer_1_out), .sel(RESET));
  Multiplexer #(.width(9), .enable("false")) multiplexer_2 (
    .in0({9{1'b1}}), .in1(9'h100), .out(multiplexer_2_out), .sel(RESET));
  and and_1 (and_1_out, d_flipflop_asc_1_q, mir_1_jam[1]);
  D_FlipFlop_Asc d_flipflop_asc_1 (
    .D(N), .CLK(CLK), .Q(d_flipflop_asc_1_q), .nPRE(1'b1), .nCLR(not_1_out));  // open: nQ
  D_FlipFlop_Asc d_flipflop_asc_2 (
    .D(Z), .CLK(CLK), .Q(d_flipflop_asc_2_q), .nPRE(1'b1), .nCLR(not_1_out));  // open: nQ
  Multiplexer #(.width(8), .enable("false")) multiplexer_3 (
    .in0(mir_1_addr), .in1(or_2_out), .out(multiplexer_3_out), .sel(mir_1_jam[2]));
  or or_1 (or_1_out[8], and_1_out, and_2_out, mir_1_addr_2[8]);
  and and_2 (and_2_out, d_flipflop_asc_2_q, mir_1_jam[0]);
  assign or_2_out = MBR | mir_1_addr;  // OR_Gate or_2, 8 bits wide
  not not_1 (not_1_out, RESET);
  MPC mpc_1 (
    .Entrada({or_1_out[8], multiplexer_3_out}), .CLK(CLK), .Salida(MPC), .nPRE(multiplexer_1_out),
    .nCLR(multiplexer_2_out));
  Control_Store control_store_1 (.CS_E(MPC), .CS_S32(control_store_1_cs_s32), .CS_S4(control_store_1_cs_s4));
  MIR mir_1 (
    .Entrada_4(control_store_1_cs_s4), .Entrada_32(control_store_1_cs_s32), .CLK(CLK), .RESET(RESET),
    .B(mir_1_b), .Mem(Mem), .C({H_C, OPC_C, TOS_C, CPP_C, LV_C, SP_C, PC_C, MDR_C, MAR_C}),
    .ALU({Shifter, ALU}), .JAM(mir_1_jam), .Addr({mir_1_addr_2[8], mir_1_addr}));
  Decoder #(.select(4), .enable("false")) decoder_1 (
    .out0(MDR_B), .out1(PC_B), .out2(MBR_B), .out3(MBRU_B), .out4(SP_B), .out5(LV_B), .out6(CPP_B),
    .out7(TOS_B), .out8(OPC_B), .sel(mir_1_b));  // open: out9, out10, out11, out12, out13, out14, out15
endmodule

module Control_Store (
  input  [8:0] CS_E,
  output [31:0] CS_S32,
  output [3:0] CS_S4
);

  ROM #(.addrWidth(9), .dataWidth(32)) rom_1 (.addr(CS_E), .data(CS_S32), .sel(1'b1));
  ROM #(.addrWidth(9), .dataWidth(4)) rom_2 (.addr(CS_E), .data(CS_S4), .sel(1'b1));

  // Notes on the sheet:
  //   Otra truchada porque Logisim no tiene
  //   un bloque de memoria mas ancho que 32 bits
  //   contents of rom_1 (hex, n*v repeats v):
  //   80000000 255*0 435021
  //   contents of rom_2 (hex, n*v repeats v):
  //   f 255*0 1
endmodule

module MPC (
  input  [8:0] nPRE,
  input  [8:0] Entrada,
  input  CLK,
  input  [8:0] nCLR,
  output [8:0] Salida
);

  D_Latch d_latch_1 (.Q(Salida[8]), .nPRE(nPRE[8]), .nCLR(nCLR[8]), .D(Entrada[8]), .CLK(CLK));  // open: nQ
  D_Latch d_latch_2 (.Q(Salida[7]), .nPRE(nPRE[7]), .nCLR(nCLR[7]), .D(Entrada[7]), .CLK(CLK));  // open: nQ
  D_Latch d_latch_3 (.Q(Salida[6]), .nPRE(nPRE[6]), .nCLR(nCLR[6]), .D(Entrada[6]), .CLK(CLK));  // open: nQ
  D_Latch d_latch_4 (.Q(Salida[5]), .nPRE(nPRE[5]), .nCLR(nCLR[5]), .D(Entrada[5]), .CLK(CLK));  // open: nQ
  D_Latch d_latch_5 (.Q(Salida[4]), .nPRE(nPRE[4]), .nCLR(nCLR[4]), .D(Entrada[4]), .CLK(CLK));  // open: nQ
  D_Latch d_latch_6 (.Q(Salida[3]), .nPRE(nPRE[3]), .nCLR(nCLR[3]), .D(Entrada[3]), .CLK(CLK));  // open: nQ
  D_Latch d_latch_7 (.Q(Salida[2]), .nPRE(nPRE[2]), .nCLR(nCLR[2]), .D(Entrada[2]), .CLK(CLK));  // open: nQ
  D_Latch d_latch_8 (.Q(Salida[1]), .nPRE(nPRE[1]), .nCLR(nCLR[1]), .D(Entrada[1]), .CLK(CLK));  // open: nQ
  D_Latch d_latch_9 (.Q(Salida[0]), .nPRE(nPRE[0]), .nCLR(nCLR[0]), .D(Entrada[0]), .CLK(CLK));  // open: nQ
endmodule

module MIR (
  input  [3:0] Entrada_4,
  input  [31:0] Entrada_32,
  input  CLK,
  input  RESET,
  output [3:0] B,
  output [2:0] Mem,
  output [8:0] C,
  output [7:0] ALU,
  output [2:0] JAM,
  output [8:0] Addr
);

  wire [3:0] multiplexer_2_out, multiplexer_4_out, not_2_out;
  wire [31:0] multiplexer_1_out, multiplexer_3_out, not_1_out;

  Multiplexer #(.width(32), .enable("false")) multiplexer_1 (
    .in0({32{1'b1}}), .in1(not_1_out), .out(multiplexer_1_out), .sel(RESET));
  assign not_1_out = ~32'h435021;  // NOT_Gate not_1, 32 bits wide
  assign not_2_out = ~4'b0001;  // NOT_Gate not_2, 4 bits wide
  Multiplexer #(.width(4), .enable("false")) multiplexer_2 (
    .in0(4'b1111), .in1(not_2_out), .out(multiplexer_2_out), .sel(RESET));
  Multiplexer #(.width(32), .enable("false")) multiplexer_3 (
    .in0({32{1'b1}}), .in1(32'h435021), .out(multiplexer_3_out), .sel(RESET));
  Multiplexer #(.width(4), .enable("false")) multiplexer_4 (
    .in0(4'b1111), .in1(4'b0001), .out(multiplexer_4_out), .sel(RESET));
  Register_32_bits_Des register_32_bits_des_1 (
    .Entrada(Entrada_32), .CLK(CLK), .Salida({Addr, JAM, ALU, C, Mem}), .nPRE(multiplexer_1_out),
    .nCLR(multiplexer_3_out));
  Register_4_bits_Des register_4_bits_des_1 (
    .Entrada(Entrada_4), .CLK(CLK), .Salida(B), .nPRE(multiplexer_2_out), .nCLR(multiplexer_4_out));
endmodule

module Data_Path (
  input  MAR_C,
  input  [31:0] MEM_RD,
  input  MDR_B,
  input  MDR_C,
  input  rd,
  input  [7:0] MEM_FETCH,
  input  PC_B,
  input  PC_C,
  input  MBR,
  input  fetch,
  input  MBRU,
  input  SP_B,
  input  SP_C,
  input  LV_B,
  input  LV_C,
  input  CPP_B,
  input  CPP_C,
  input  RESET,
  input  TOS_B,
  input  TOS_C,
  input  OPC_B,
  input  OPC_C,
  input  H_C,
  input  INVA,
  input  ENA,
  input  CLK,
  input  ENB,
  input  INC,
  input  [1:0] F,
  input  SRA1,
  input  SLL8,
  output [31:0] MEM_MAR,
  output [31:0] MEM_WR,
  output [31:0] MEM_PC,
  output [7:0] OP_CODE,
  output [31:0] B,
  output Z,
  output N,
  output [31:0] C
);

  wire [7:0] multiplexer_1_out;
  wire [31:0] alu_32_bits_1_out_10, multiplexer_2_out, multiplexer_3_out,
       register_32_bits_hold_paralel_load_1_salida, register_32_bits_hold_paralel_load_4_salida,
       register_32_bits_hold_paralel_load_5_salida, register_32_bits_hold_paralel_load_6_salida,
       register_32_bits_hold_paralel_load_7_salida, register_32_bits_hold_paralel_load_8_salida,
       register_32_bits_hold_paralel_load_9_salida;

  Multiplexer #(.width(8), .enable("false")) multiplexer_1 (
    .in0({8{1'b1}}), .in1({8{1'b0}}), .out(multiplexer_1_out), .sel(RESET));
  Multiplexer #(.width(32), .enable("false")) multiplexer_2 (
    .in0({32{1'b1}}), .in1({32{1'b0}}), .out(multiplexer_2_out), .sel(RESET));
  Multiplexer #(.width(32), .enable("false")) multiplexer_3 (.in0(C), .in1(MEM_RD), .out(multiplexer_3_out), .sel(rd));
  Register_8_bits_Hold___Paralel_Load register_8_bits_hold_paralel_load_1 (
    .Entrada(MEM_FETCH), .LOAD(fetch), .CLK(CLK), .Salida(OP_CODE), .nPRE({8{1'b1}}), .nCLR(multiplexer_1_out));
  Register_32_bits_Hold___Paralel_Load register_32_bits_hold_paralel_load_1 (
    .Entrada(C), .LOAD(MAR_C), .nPRE({32{1'b1}}), .CLK(CLK),
    .Salida(register_32_bits_hold_paralel_load_1_salida), .nCLR(multiplexer_2_out));
  Register_32_bits_Hold___Paralel_Load register_32_bits_hold_paralel_load_2 (
    .Entrada(multiplexer_3_out), .LOAD(MDR_C), .nPRE({32{1'b1}}), .CLK(CLK), .Salida(MEM_WR),
    .nCLR(multiplexer_2_out));
  assign B = MDR_B ? MEM_WR : 32'bz;  // Controlled_Buffer controlled_buffer_1
  assign B = PC_B ? MEM_PC : 32'bz;  // Controlled_Buffer controlled_buffer_2
  Register_32_bits_Hold___Paralel_Load register_32_bits_hold_paralel_load_3 (
    .Entrada(C), .LOAD(PC_C), .nPRE({32{1'b1}}), .CLK(CLK), .Salida(MEM_PC), .nCLR(multiplexer_2_out));
  MBR_EN mbr_en_1 (.in_1(OP_CODE), .Salida_Signada(B), .Salida_No_Signada(B), .MRB(MBR), .MBRU(MBRU));
  Register_32_bits_Hold___Paralel_Load register_32_bits_hold_paralel_load_4 (
    .Entrada(C), .LOAD(SP_C), .nPRE({32{1'b1}}), .CLK(CLK),
    .Salida(register_32_bits_hold_paralel_load_4_salida), .nCLR(multiplexer_2_out));
  assign B = SP_B ? register_32_bits_hold_paralel_load_4_salida : 32'bz;  // Controlled_Buffer controlled_buffer_3
  assign B = LV_B ? register_32_bits_hold_paralel_load_5_salida : 32'bz;  // Controlled_Buffer controlled_buffer_4
  Register_32_bits_Hold___Paralel_Load register_32_bits_hold_paralel_load_5 (
    .Entrada(C), .LOAD(LV_C), .nPRE({32{1'b1}}), .CLK(CLK),
    .Salida(register_32_bits_hold_paralel_load_5_salida), .nCLR(multiplexer_2_out));
  assign B = CPP_B ? register_32_bits_hold_paralel_load_6_salida : 32'bz;  // Controlled_Buffer controlled_buffer_5
  Register_32_bits_Hold___Paralel_Load register_32_bits_hold_paralel_load_6 (
    .Entrada(C), .LOAD(CPP_C), .nPRE({32{1'b1}}), .CLK(CLK),
    .Salida(register_32_bits_hold_paralel_load_6_salida), .nCLR(multiplexer_2_out));
  assign B = TOS_B ? register_32_bits_hold_paralel_load_7_salida : 32'bz;  // Controlled_Buffer controlled_buffer_6
  Register_32_bits_Hold___Paralel_Load register_32_bits_hold_paralel_load_7 (
    .Entrada(C), .LOAD(TOS_C), .nPRE({32{1'b1}}), .CLK(CLK),
    .Salida(register_32_bits_hold_paralel_load_7_salida), .nCLR(multiplexer_2_out));
  assign B = OPC_B ? register_32_bits_hold_paralel_load_8_salida : 32'bz;  // Controlled_Buffer controlled_buffer_7
  Register_32_bits_Hold___Paralel_Load register_32_bits_hold_paralel_load_8 (
    .Entrada(C), .LOAD(OPC_C), .nPRE({32{1'b1}}), .CLK(CLK),
    .Salida(register_32_bits_hold_paralel_load_8_salida), .nCLR(multiplexer_2_out));
  Register_32_bits_Hold___Paralel_Load register_32_bits_hold_paralel_load_9 (
    .Entrada(C), .LOAD(H_C), .nPRE({32{1'b1}}), .CLK(CLK),
    .Salida(register_32_bits_hold_paralel_load_9_salida), .nCLR(multiplexer_2_out));
  MAR mar_1 (.in_1(register_32_bits_hold_paralel_load_1_salida), .out_2(MEM_MAR));
  Desplazador desplazador_1 (.SRA1(SRA1), .SLL8(SLL8), .Entrada(alu_32_bits_1_out_10), .Salida(C));
  ALU_32_bits alu_32_bits_1 (
    .in_1(INVA), .in_2(ENA), .in_3(ENB), .in_6(F), .Carry_in(INC),
    .A(register_32_bits_hold_paralel_load_9_salida), .B(B), .out_10(alu_32_bits_1_out_10), .Z(Z), .N(N));  // open: out_9

  // Notes on the sheet:
  //   Preset 8 Bits
  //   Clear 8 Bits
  //   Preset 32 Bits
  //   Clear 32 Bits
  //   Bus B
  //   Bus C
endmodule

module Register_32_bits_Hold___Paralel_Load (
  input  [31:0] nPRE,
  input  [31:0] Entrada,
  input  LOAD,
  input  CLK,
  input  [31:0] nCLR,
  output [31:0] Salida
);

  wire [31:0] multiplexer_1_out;

  Multiplexer #(.width(32), .enable("false")) multiplexer_1 (
    .in0(Salida), .in1(Entrada), .out(multiplexer_1_out), .sel(LOAD));
  D_FlipFlop_Des d_flipflop_des_1 (
    .D(multiplexer_1_out[31]), .CLK(CLK), .Q(Salida[31]), .nPRE(nPRE[31]), .nCLR(nCLR[31]));  // open: nQ
  D_FlipFlop_Des d_flipflop_des_2 (
    .D(multiplexer_1_out[30]), .CLK(CLK), .Q(Salida[30]), .nPRE(nPRE[30]), .nCLR(nCLR[30]));  // open: nQ
  D_FlipFlop_Des d_flipflop_des_3 (
    .D(multiplexer_1_out[29]), .CLK(CLK), .Q(Salida[29]), .nPRE(nPRE[29]), .nCLR(nCLR[29]));  // open: nQ
  D_FlipFlop_Des d_flipflop_des_4 (
    .D(multiplexer_1_out[28]), .CLK(CLK), .Q(Salida[28]), .nPRE(nPRE[28]), .nCLR(nCLR[28]));  // open: nQ
  D_FlipFlop_Des d_flipflop_des_5 (
    .D(multiplexer_1_out[27]), .CLK(CLK), .Q(Salida[27]), .nPRE(nPRE[27]), .nCLR(nCLR[27]));  // open: nQ
  D_FlipFlop_Des d_flipflop_des_6 (
    .D(multiplexer_1_out[26]), .CLK(CLK), .Q(Salida[26]), .nPRE(nPRE[26]), .nCLR(nCLR[26]));  // open: nQ
  D_FlipFlop_Des d_flipflop_des_7 (
    .D(multiplexer_1_out[25]), .CLK(CLK), .Q(Salida[25]), .nPRE(nPRE[25]), .nCLR(nCLR[25]));  // open: nQ
  D_FlipFlop_Des d_flipflop_des_8 (
    .D(multiplexer_1_out[24]), .CLK(CLK), .Q(Salida[24]), .nPRE(nPRE[24]), .nCLR(nCLR[24]));  // open: nQ
  D_FlipFlop_Des d_flipflop_des_9 (
    .D(multiplexer_1_out[23]), .CLK(CLK), .Q(Salida[23]), .nPRE(nPRE[23]), .nCLR(nCLR[23]));  // open: nQ
  D_FlipFlop_Des d_flipflop_des_10 (
    .D(multiplexer_1_out[22]), .CLK(CLK), .Q(Salida[22]), .nPRE(nPRE[22]), .nCLR(nCLR[22]));  // open: nQ
  D_FlipFlop_Des d_flipflop_des_11 (
    .D(multiplexer_1_out[21]), .CLK(CLK), .Q(Salida[21]), .nPRE(nPRE[21]), .nCLR(nCLR[21]));  // open: nQ
  D_FlipFlop_Des d_flipflop_des_12 (
    .D(multiplexer_1_out[20]), .CLK(CLK), .Q(Salida[20]), .nPRE(nPRE[20]), .nCLR(nCLR[20]));  // open: nQ
  D_FlipFlop_Des d_flipflop_des_13 (
    .D(multiplexer_1_out[19]), .CLK(CLK), .Q(Salida[19]), .nPRE(nPRE[19]), .nCLR(nCLR[19]));  // open: nQ
  D_FlipFlop_Des d_flipflop_des_14 (
    .D(multiplexer_1_out[18]), .CLK(CLK), .Q(Salida[18]), .nPRE(nPRE[18]), .nCLR(nCLR[18]));  // open: nQ
  D_FlipFlop_Des d_flipflop_des_15 (
    .D(multiplexer_1_out[17]), .CLK(CLK), .Q(Salida[17]), .nPRE(nPRE[17]), .nCLR(nCLR[17]));  // open: nQ
  D_FlipFlop_Des d_flipflop_des_16 (
    .D(multiplexer_1_out[16]), .CLK(CLK), .Q(Salida[16]), .nPRE(nPRE[16]), .nCLR(nCLR[16]));  // open: nQ
  D_FlipFlop_Des d_flipflop_des_17 (
    .D(multiplexer_1_out[15]), .CLK(CLK), .Q(Salida[15]), .nPRE(nPRE[15]), .nCLR(nCLR[15]));  // open: nQ
  D_FlipFlop_Des d_flipflop_des_18 (
    .D(multiplexer_1_out[14]), .CLK(CLK), .Q(Salida[14]), .nPRE(nPRE[14]), .nCLR(nCLR[14]));  // open: nQ
  D_FlipFlop_Des d_flipflop_des_19 (
    .D(multiplexer_1_out[13]), .CLK(CLK), .Q(Salida[13]), .nPRE(nPRE[13]), .nCLR(nCLR[13]));  // open: nQ
  D_FlipFlop_Des d_flipflop_des_20 (
    .D(multiplexer_1_out[12]), .CLK(CLK), .Q(Salida[12]), .nPRE(nPRE[12]), .nCLR(nCLR[12]));  // open: nQ
  D_FlipFlop_Des d_flipflop_des_21 (
    .D(multiplexer_1_out[11]), .CLK(CLK), .Q(Salida[11]), .nPRE(nPRE[11]), .nCLR(nCLR[11]));  // open: nQ
  D_FlipFlop_Des d_flipflop_des_22 (
    .D(multiplexer_1_out[10]), .CLK(CLK), .Q(Salida[10]), .nPRE(nPRE[10]), .nCLR(nCLR[10]));  // open: nQ
  D_FlipFlop_Des d_flipflop_des_23 (
    .D(multiplexer_1_out[9]), .CLK(CLK), .Q(Salida[9]), .nPRE(nPRE[9]), .nCLR(nCLR[9]));  // open: nQ
  D_FlipFlop_Des d_flipflop_des_24 (
    .D(multiplexer_1_out[8]), .CLK(CLK), .Q(Salida[8]), .nPRE(nPRE[8]), .nCLR(nCLR[8]));  // open: nQ
  D_FlipFlop_Des d_flipflop_des_25 (
    .D(multiplexer_1_out[7]), .CLK(CLK), .Q(Salida[7]), .nPRE(nPRE[7]), .nCLR(nCLR[7]));  // open: nQ
  D_FlipFlop_Des d_flipflop_des_26 (
    .D(multiplexer_1_out[6]), .CLK(CLK), .Q(Salida[6]), .nPRE(nPRE[6]), .nCLR(nCLR[6]));  // open: nQ
  D_FlipFlop_Des d_flipflop_des_27 (
    .D(multiplexer_1_out[5]), .CLK(CLK), .Q(Salida[5]), .nPRE(nPRE[5]), .nCLR(nCLR[5]));  // open: nQ
  D_FlipFlop_Des d_flipflop_des_28 (
    .D(multiplexer_1_out[4]), .CLK(CLK), .Q(Salida[4]), .nPRE(nPRE[4]), .nCLR(nCLR[4]));  // open: nQ
  D_FlipFlop_Des d_flipflop_des_29 (
    .D(multiplexer_1_out[3]), .CLK(CLK), .Q(Salida[3]), .nPRE(nPRE[3]), .nCLR(nCLR[3]));  // open: nQ
  D_FlipFlop_Des d_flipflop_des_30 (
    .D(multiplexer_1_out[2]), .CLK(CLK), .Q(Salida[2]), .nPRE(nPRE[2]), .nCLR(nCLR[2]));  // open: nQ
  D_FlipFlop_Des d_flipflop_des_31 (
    .D(multiplexer_1_out[1]), .CLK(CLK), .Q(Salida[1]), .nPRE(nPRE[1]), .nCLR(nCLR[1]));  // open: nQ
  D_FlipFlop_Des d_flipflop_des_32 (
    .D(multiplexer_1_out[0]), .CLK(CLK), .Q(Salida[0]), .nPRE(nPRE[0]), .nCLR(nCLR[0]));  // open: nQ
endmodule

module Register_32_bits_Des (
  input  [31:0] nPRE,
  input  [31:0] Entrada,
  input  CLK,
  input  [31:0] nCLR,
  output [31:0] Salida
);

  D_FlipFlop_Des d_flipflop_des_1 (
    .D(Entrada[31]), .CLK(CLK), .Q(Salida[31]), .nPRE(nPRE[31]), .nCLR(nCLR[31]));  // open: nQ
  D_FlipFlop_Des d_flipflop_des_2 (
    .D(Entrada[30]), .CLK(CLK), .Q(Salida[30]), .nPRE(nPRE[30]), .nCLR(nCLR[30]));  // open: nQ
  D_FlipFlop_Des d_flipflop_des_3 (
    .D(Entrada[29]), .CLK(CLK), .Q(Salida[29]), .nPRE(nPRE[29]), .nCLR(nCLR[29]));  // open: nQ
  D_FlipFlop_Des d_flipflop_des_4 (
    .D(Entrada[28]), .CLK(CLK), .Q(Salida[28]), .nPRE(nPRE[28]), .nCLR(nCLR[28]));  // open: nQ
  D_FlipFlop_Des d_flipflop_des_5 (
    .D(Entrada[27]), .CLK(CLK), .Q(Salida[27]), .nPRE(nPRE[27]), .nCLR(nCLR[27]));  // open: nQ
  D_FlipFlop_Des d_flipflop_des_6 (
    .D(Entrada[26]), .CLK(CLK), .Q(Salida[26]), .nPRE(nPRE[26]), .nCLR(nCLR[26]));  // open: nQ
  D_FlipFlop_Des d_flipflop_des_7 (
    .D(Entrada[25]), .CLK(CLK), .Q(Salida[25]), .nPRE(nPRE[25]), .nCLR(nCLR[25]));  // open: nQ
  D_FlipFlop_Des d_flipflop_des_8 (
    .D(Entrada[24]), .CLK(CLK), .Q(Salida[24]), .nPRE(nPRE[24]), .nCLR(nCLR[24]));  // open: nQ
  D_FlipFlop_Des d_flipflop_des_9 (
    .D(Entrada[23]), .CLK(CLK), .Q(Salida[23]), .nPRE(nPRE[23]), .nCLR(nCLR[23]));  // open: nQ
  D_FlipFlop_Des d_flipflop_des_10 (
    .D(Entrada[22]), .CLK(CLK), .Q(Salida[22]), .nPRE(nPRE[22]), .nCLR(nCLR[22]));  // open: nQ
  D_FlipFlop_Des d_flipflop_des_11 (
    .D(Entrada[21]), .CLK(CLK), .Q(Salida[21]), .nPRE(nPRE[21]), .nCLR(nCLR[21]));  // open: nQ
  D_FlipFlop_Des d_flipflop_des_12 (
    .D(Entrada[20]), .CLK(CLK), .Q(Salida[20]), .nPRE(nPRE[20]), .nCLR(nCLR[20]));  // open: nQ
  D_FlipFlop_Des d_flipflop_des_13 (
    .D(Entrada[19]), .CLK(CLK), .Q(Salida[19]), .nPRE(nPRE[19]), .nCLR(nCLR[19]));  // open: nQ
  D_FlipFlop_Des d_flipflop_des_14 (
    .D(Entrada[18]), .CLK(CLK), .Q(Salida[18]), .nPRE(nPRE[18]), .nCLR(nCLR[18]));  // open: nQ
  D_FlipFlop_Des d_flipflop_des_15 (
    .D(Entrada[17]), .CLK(CLK), .Q(Salida[17]), .nPRE(nPRE[17]), .nCLR(nCLR[17]));  // open: nQ
  D_FlipFlop_Des d_flipflop_des_16 (
    .D(Entrada[16]), .CLK(CLK), .Q(Salida[16]), .nPRE(nPRE[16]), .nCLR(nCLR[16]));  // open: nQ
  D_FlipFlop_Des d_flipflop_des_17 (
    .D(Entrada[15]), .CLK(CLK), .Q(Salida[15]), .nPRE(nPRE[15]), .nCLR(nCLR[15]));  // open: nQ
  D_FlipFlop_Des d_flipflop_des_18 (
    .D(Entrada[14]), .CLK(CLK), .Q(Salida[14]), .nPRE(nPRE[14]), .nCLR(nCLR[14]));  // open: nQ
  D_FlipFlop_Des d_flipflop_des_19 (
    .D(Entrada[13]), .CLK(CLK), .Q(Salida[13]), .nPRE(nPRE[13]), .nCLR(nCLR[13]));  // open: nQ
  D_FlipFlop_Des d_flipflop_des_20 (
    .D(Entrada[12]), .CLK(CLK), .Q(Salida[12]), .nPRE(nPRE[12]), .nCLR(nCLR[12]));  // open: nQ
  D_FlipFlop_Des d_flipflop_des_21 (
    .D(Entrada[11]), .CLK(CLK), .Q(Salida[11]), .nPRE(nPRE[11]), .nCLR(nCLR[11]));  // open: nQ
  D_FlipFlop_Des d_flipflop_des_22 (
    .D(Entrada[10]), .CLK(CLK), .Q(Salida[10]), .nPRE(nPRE[10]), .nCLR(nCLR[10]));  // open: nQ
  D_FlipFlop_Des d_flipflop_des_23 (
    .D(Entrada[9]), .CLK(CLK), .Q(Salida[9]), .nPRE(nPRE[9]), .nCLR(nCLR[9]));  // open: nQ
  D_FlipFlop_Des d_flipflop_des_24 (
    .D(Entrada[8]), .CLK(CLK), .Q(Salida[8]), .nPRE(nPRE[8]), .nCLR(nCLR[8]));  // open: nQ
  D_FlipFlop_Des d_flipflop_des_25 (
    .D(Entrada[7]), .CLK(CLK), .Q(Salida[7]), .nPRE(nPRE[7]), .nCLR(nCLR[7]));  // open: nQ
  D_FlipFlop_Des d_flipflop_des_26 (
    .D(Entrada[6]), .CLK(CLK), .Q(Salida[6]), .nPRE(nPRE[6]), .nCLR(nCLR[6]));  // open: nQ
  D_FlipFlop_Des d_flipflop_des_27 (
    .D(Entrada[5]), .CLK(CLK), .Q(Salida[5]), .nPRE(nPRE[5]), .nCLR(nCLR[5]));  // open: nQ
  D_FlipFlop_Des d_flipflop_des_28 (
    .D(Entrada[4]), .CLK(CLK), .Q(Salida[4]), .nPRE(nPRE[4]), .nCLR(nCLR[4]));  // open: nQ
  D_FlipFlop_Des d_flipflop_des_29 (
    .D(Entrada[3]), .CLK(CLK), .Q(Salida[3]), .nPRE(nPRE[3]), .nCLR(nCLR[3]));  // open: nQ
  D_FlipFlop_Des d_flipflop_des_30 (
    .D(Entrada[2]), .CLK(CLK), .Q(Salida[2]), .nPRE(nPRE[2]), .nCLR(nCLR[2]));  // open: nQ
  D_FlipFlop_Des d_flipflop_des_31 (
    .D(Entrada[1]), .CLK(CLK), .Q(Salida[1]), .nPRE(nPRE[1]), .nCLR(nCLR[1]));  // open: nQ
  D_FlipFlop_Des d_flipflop_des_32 (
    .D(Entrada[0]), .CLK(CLK), .Q(Salida[0]), .nPRE(nPRE[0]), .nCLR(nCLR[0]));  // open: nQ
endmodule

module Register_8_bits_Hold___Paralel_Load (
  input  [7:0] nPRE,
  input  [7:0] Entrada,
  input  LOAD,
  input  CLK,
  input  [7:0] nCLR,
  output [7:0] Salida
);

  wire [7:0] multiplexer_1_out;

  Multiplexer #(.width(8), .enable("false")) multiplexer_1 (
    .in0(Salida), .in1(Entrada), .out(multiplexer_1_out), .sel(LOAD));
  D_FlipFlop_Des d_flipflop_des_1 (
    .D(multiplexer_1_out[7]), .CLK(CLK), .Q(Salida[7]), .nPRE(nPRE[7]), .nCLR(nCLR[7]));  // open: nQ
  D_FlipFlop_Des d_flipflop_des_2 (
    .D(multiplexer_1_out[6]), .CLK(CLK), .Q(Salida[6]), .nPRE(nPRE[6]), .nCLR(nCLR[6]));  // open: nQ
  D_FlipFlop_Des d_flipflop_des_3 (
    .D(multiplexer_1_out[5]), .CLK(CLK), .Q(Salida[5]), .nPRE(nPRE[5]), .nCLR(nCLR[5]));  // open: nQ
  D_FlipFlop_Des d_flipflop_des_4 (
    .D(multiplexer_1_out[4]), .CLK(CLK), .Q(Salida[4]), .nPRE(nPRE[4]), .nCLR(nCLR[4]));  // open: nQ
  D_FlipFlop_Des d_flipflop_des_5 (
    .D(multiplexer_1_out[3]), .CLK(CLK), .Q(Salida[3]), .nPRE(nPRE[3]), .nCLR(nCLR[3]));  // open: nQ
  D_FlipFlop_Des d_flipflop_des_6 (
    .D(multiplexer_1_out[2]), .CLK(CLK), .Q(Salida[2]), .nPRE(nPRE[2]), .nCLR(nCLR[2]));  // open: nQ
  D_FlipFlop_Des d_flipflop_des_7 (
    .D(multiplexer_1_out[1]), .CLK(CLK), .Q(Salida[1]), .nPRE(nPRE[1]), .nCLR(nCLR[1]));  // open: nQ
  D_FlipFlop_Des d_flipflop_des_8 (
    .D(multiplexer_1_out[0]), .CLK(CLK), .Q(Salida[0]), .nPRE(nPRE[0]), .nCLR(nCLR[0]));  // open: nQ
endmodule

module Register_4_bits_Des (
  input  [3:0] nPRE,
  input  [3:0] Entrada,
  input  CLK,
  input  [3:0] nCLR,
  output [3:0] Salida
);

  D_FlipFlop_Des d_flipflop_des_1 (
    .D(Entrada[3]), .CLK(CLK), .Q(Salida[3]), .nPRE(nPRE[3]), .nCLR(nCLR[3]));  // open: nQ
  D_FlipFlop_Des d_flipflop_des_2 (
    .D(Entrada[2]), .CLK(CLK), .Q(Salida[2]), .nPRE(nPRE[2]), .nCLR(nCLR[2]));  // open: nQ
  D_FlipFlop_Des d_flipflop_des_3 (
    .D(Entrada[1]), .CLK(CLK), .Q(Salida[1]), .nPRE(nPRE[1]), .nCLR(nCLR[1]));  // open: nQ
  D_FlipFlop_Des d_flipflop_des_4 (
    .D(Entrada[0]), .CLK(CLK), .Q(Salida[0]), .nPRE(nPRE[0]), .nCLR(nCLR[0]));  // open: nQ
endmodule

module MAR (
  input  [31:0] in_1,
  output [31:0] out_2
);


  assign out_2 = {in_1[29:0], 2'b00};
endmodule

module MBR_EN (
  input  [7:0] in_1,
  input  MRB,
  input  MBRU,
  output [31:0] Salida_Signada,
  output [31:0] Salida_No_Signada
);

  assign Salida_Signada = MRB ? {{25{in_1[7]}}, in_1[6:0]} : 32'bz;  // Controlled_Buffer controlled_buffer_1
  assign Salida_No_Signada = MBRU ? {{24{1'b0}}, in_1} : 32'bz;  // Controlled_Buffer controlled_buffer_2
endmodule

module D_FlipFlop_Des (
  input  nPRE,
  input  D,
  input  CLK,
  input  nCLR,
  output Q,
  output nQ
);

  wire d_latch_1_q, not_1_out;

  D_Latch d_latch_1 (.Q(d_latch_1_q), .nPRE(nPRE), .nCLR(nCLR), .D(D), .CLK(CLK));  // open: nQ
  not not_1 (not_1_out, CLK);
  D_Latch d_latch_2 (.Q(Q), .nQ(nQ), .nPRE(nPRE), .nCLR(nCLR), .D(d_latch_1_q), .CLK(not_1_out));
endmodule

module D_FlipFlop_Asc (
  input  nPRE,
  input  D,
  input  CLK,
  input  nCLR,
  output Q,
  output nQ
);

  wire d_latch_1_nq, not_1_out;

  not not_1 (not_1_out, CLK);
  D_Latch d_latch_1 (.nQ(d_latch_1_nq), .nPRE(nPRE), .nCLR(nCLR), .D(D), .CLK(not_1_out));  // open: Q
  D_Latch d_latch_2 (.Q(Q), .nQ(nQ), .nPRE(nPRE), .nCLR(nCLR), .D(d_latch_1_nq), .CLK(CLK));
endmodule

module D_Latch (
  input  nPRE,
  input  D,
  input  CLK,
  input  nCLR,
  output Q,
  output nQ
);

  wire nand_1_out, nand_2_out, not_1_out;

  not not_1 (not_1_out, D);
  nand nand_1 (nand_1_out, D, CLK);
  nand nand_2 (nand_2_out, CLK, not_1_out);
  nand nand_3 (Q, nand_1_out, nPRE, nQ);
  nand nand_4 (nQ, Q, nCLR, nand_2_out);
endmodule

module ALU_1_bit (
  input  Cin,
  input  INVA,
  input  A,
  input  ENA,
  input  B,
  input  ENB,
  input  [1:0] F,
  output Salida,
  output Cout
);

  wire and_1_out, and_2_out, and_3_out, and_4_out, and_5_out, and_6_out, sumador_completo_alu_1_s,
       unidad_logica_alu_1_and, unidad_logica_alu_1_not, unidad_logica_alu_1_or, xor_1_out;

  and and_1 (and_1_out, A, ENA);
  and and_2 (and_2_out, B, ENB);
  xor xor_1 (xor_1_out, INVA, and_1_out);
  and and_3 (and_3_out, ~F[0], ~F[1]);  // AND_Gate
  and and_4 (and_4_out, ~F[0], F[1]);  // AND_Gate
  and and_5 (and_5_out, F[0], ~F[1]);  // AND_Gate
  and and_6 (and_6_out, F[0], F[1]);
  Unidad_Logica__ALU unidad_logica_alu_1 (
    .A(xor_1_out), .AND(unidad_logica_alu_1_and), .B(and_2_out), .OR(unidad_logica_alu_1_or),
    .NOT(unidad_logica_alu_1_not), .EN1(and_3_out), .EN2(and_4_out), .EN3(and_5_out));
  Sumador_Completo__ALU sumador_completo_alu_1 (
    .Cin(Cin), .A(xor_1_out), .S(sumador_completo_alu_1_s), .B(and_2_out), .EN(and_6_out), .Cout(Cout));
  or or_1 (Salida, unidad_logica_alu_1_and, unidad_logica_alu_1_or, unidad_logica_alu_1_not, sumador_completo_alu_1_s);
endmodule

module ALU_2_bits (
  input  in_1,
  input  [1:0] A,
  input  [1:0] B,
  input  in_4,
  input  in_5,
  input  [1:0] in_6,
  input  Carry_in,
  output out_8,
  output out_9,
  output out_10
);

  wire alu_1_bit_2_cout;

  ALU_1_bit alu_1_bit_1 (
    .Cin(alu_1_bit_2_cout), .INVA(in_1), .A(A[1]), .Salida(out_9), .ENA(in_4), .B(B[1]), .ENB(in_5),
    .F(in_6), .Cout(out_8));
  ALU_1_bit alu_1_bit_2 (
    .Cin(Carry_in), .INVA(in_1), .A(A[0]), .Salida(out_10), .ENA(in_4), .B(B[0]), .ENB(in_5), .F(in_6),
    .Cout(alu_1_bit_2_cout));

  // Other names for the same wires on the sheet: ENA = in_4; ENB = in_5; F[1:0] = in_6; INVA = in_1
endmodule

module ALU_4_bits (
  input  in_1,
  input  [3:0] A,
  input  [3:0] B,
  input  in_4,
  input  in_5,
  input  [1:0] in_6,
  input  Carry_in,
  output out_8,
  output out_9,
  output out_10,
  output out_11,
  output out_12
);

  wire alu_2_bits_2_out_8;

  ALU_2_bits alu_2_bits_1 (
    .in_1(in_1), .in_4(in_4), .in_5(in_5), .in_6(in_6), .out_8(out_8), .Carry_in(alu_2_bits_2_out_8),
    .A(A[3:2]), .B(B[3:2]), .out_9(out_9), .out_10(out_10));
  ALU_2_bits alu_2_bits_2 (
    .in_1(in_1), .in_4(in_4), .in_5(in_5), .in_6(in_6), .out_8(alu_2_bits_2_out_8), .Carry_in(Carry_in),
    .A(A[1:0]), .B(B[1:0]), .out_9(out_11), .out_10(out_12));

  // Other names for the same wires on the sheet: ENA = in_4; ENB = in_5; F[1:0] = in_6; INVA = in_1
endmodule

module ALU_8_bits (
  input  in_1,
  input  [7:0] A,
  input  [7:0] B,
  input  in_4,
  input  in_5,
  input  [1:0] in_6,
  input  Carry_in,
  output out_8,
  output out_9,
  output out_10,
  output out_11,
  output out_12,
  output out_13,
  output out_14,
  output out_15,
  output out_16
);

  wire alu_4_bits_2_out_8;

  ALU_4_bits alu_4_bits_1 (
    .in_1(in_1), .in_4(in_4), .in_5(in_5), .in_6(in_6), .out_8(out_8), .Carry_in(alu_4_bits_2_out_8),
    .A(A[7:4]), .B(B[7:4]), .out_9(out_9), .out_10(out_10), .out_11(out_11), .out_12(out_12));
  ALU_4_bits alu_4_bits_2 (
    .in_1(in_1), .in_4(in_4), .in_5(in_5), .in_6(in_6), .out_8(alu_4_bits_2_out_8), .Carry_in(Carry_in),
    .A(A[3:0]), .B(B[3:0]), .out_9(out_13), .out_10(out_14), .out_11(out_15), .out_12(out_16));

  // Other names for the same wires on the sheet: ENA = in_4; ENB = in_5; F[1:0] = in_6; INVA = in_1
endmodule

module ALU_16_bits (
  input  in_1,
  input  in_2,
  input  [15:0] A,
  input  [15:0] B,
  input  in_5,
  input  [1:0] in_6,
  input  Carry_in,
  output out_8,
  output [15:0] out_9
);

  wire alu_8_bits_2_out_8;

  ALU_8_bits alu_8_bits_1 (
    .in_1(in_1), .in_4(in_2), .in_5(in_5), .in_6(in_6), .out_8(out_8), .Carry_in(alu_8_bits_2_out_8),
    .A(A[15:8]), .B(B[15:8]), .out_9(out_9[15]), .out_10(out_9[14]), .out_11(out_9[13]), .out_12(out_9[12]),
    .out_13(out_9[11]), .out_14(out_9[10]), .out_15(out_9[9]), .out_16(out_9[8]));
  ALU_8_bits alu_8_bits_2 (
    .in_1(in_1), .in_4(in_2), .in_5(in_5), .in_6(in_6), .out_8(alu_8_bits_2_out_8), .Carry_in(Carry_in),
    .A(A[7:0]), .B(B[7:0]), .out_9(out_9[7]), .out_10(out_9[6]), .out_11(out_9[5]), .out_12(out_9[4]),
    .out_13(out_9[3]), .out_14(out_9[2]), .out_15(out_9[1]), .out_16(out_9[0]));

  // Other names for the same wires on the sheet: ENA = in_2; ENB = in_5; F[1:0] = in_6; INVA = in_1
endmodule

module ALU_32_bits (
  input  in_1,
  input  in_2,
  input  in_3,
  input  [31:0] A,
  input  [31:0] B,
  input  [1:0] in_6,
  input  Carry_in,
  output Z,
  output out_9,
  output [31:0] out_10,
  output N
);

  wire alu_16_bits_2_out_8;

  ALU_16_bits alu_16_bits_1 (
    .in_1(in_1), .in_2(in_2), .in_5(in_3), .in_6(in_6), .out_8(out_9), .Carry_in(alu_16_bits_2_out_8),
    .A(A[31:16]), .B(B[31:16]), .out_9({N, out_10[30:16]}));
  ALU_16_bits alu_16_bits_2 (
    .in_1(in_1), .in_2(in_2), .in_5(in_3), .in_6(in_6), .out_8(alu_16_bits_2_out_8), .Carry_in(Carry_in),
    .A(A[15:0]), .B(B[15:0]), .out_9(out_10[15:0]));
  nor nor_1 (Z, out_10[0], out_10[1], out_10[2], out_10[3], out_10[4], out_10[5], out_10[6], out_10[7], out_10[8], out_10[9], out_10[10], out_10[11], out_10[12], out_10[13], out_10[14], out_10[15], out_10[17], out_10[18], out_10[19], out_10[20], out_10[21], out_10[22], out_10[23], out_10[24], out_10[25], out_10[26], out_10[27], out_10[28], out_10[29], out_10[30], N, out_10[16]);

  assign out_10[31] = N;

  // Other names for the same wires on the sheet: ENA = in_2; ENB = in_3; F[1:0] = in_6; INVA = in_1
endmodule

module Unidad_Logica__ALU (
  input  A,
  input  B,
  input  EN1,
  input  EN2,
  input  EN3,
  output AND,
  output OR,
  output NOT
);

  wire and_1_out, not_1_out, or_1_out;

  and and_1 (and_1_out, A, B);
  or or_1 (or_1_out, A, B);
  not not_1 (not_1_out, B);
  and and_2 (AND, and_1_out, EN1);
  and and_3 (OR, or_1_out, EN2);
  and and_4 (NOT, not_1_out, EN3);
endmodule

module Sumador_Completo__ALU (
  input  Cin,
  input  A,
  input  B,
  input  EN,
  output S,
  output Cout
);

  wire and_1_out, and_2_out, and_3_out, and_4_out, xor_1_out;

  and and_1 (and_1_out, A, EN);
  and and_2 (and_2_out, B, EN);
  and and_3 (and_3_out, and_1_out, and_2_out);
  or or_1 (Cout, and_3_out, and_4_out);
  xor xor_1 (xor_1_out, and_1_out, and_2_out);
  and and_4 (and_4_out, xor_1_out, Cin);
  xor xor_2 (S, Cin, xor_1_out);
endmodule

module Desplazador (
  input  [31:0] Entrada,
  input  SLL8,
  input  SRA1,
  output [31:0] Salida
);

  wire and_1_out, and_2_out, and_3_out, and_4_out, and_5_out, and_6_out, and_7_out, and_8_out, and_9_out,
       and_10_out, and_11_out, and_12_out, and_13_out, and_14_out, and_15_out, and_16_out, and_17_out,
       and_18_out, and_19_out, and_20_out, and_21_out, and_22_out, and_23_out, and_24_out, and_25_out,
       and_26_out, and_27_out, and_28_out, and_29_out, and_30_out, and_31_out, and_32_out, and_33_out,
       and_34_out, and_35_out, and_36_out, and_37_out, and_38_out, and_39_out, and_40_out, and_41_out,
       and_42_out, and_43_out, and_44_out, and_45_out, and_46_out, and_47_out, and_48_out, and_49_out,
       and_50_out, and_51_out, and_52_out, and_53_out, and_54_out, and_55_out, and_56_out, and_57_out,
       and_58_out, and_59_out, and_60_out, and_61_out, and_62_out, and_63_out, and_64_out, and_65_out,
       and_66_out, and_67_out, and_68_out, and_69_out, and_70_out, and_71_out, and_72_out, and_73_out,
       and_74_out, and_75_out, and_76_out, and_77_out, and_78_out, and_79_out, and_80_out, and_81_out,
       and_82_out, and_83_out, and_84_out, and_85_out, and_86_out, and_87_out, nor_1_out;

  nor nor_1 (nor_1_out, SLL8, SRA1);
  and and_1 (and_1_out, Entrada[31], SRA1);
  and and_2 (and_2_out, nor_1_out, Entrada[31]);
  or or_1 (Salida[31], and_1_out, and_2_out, and_18_out);
  and and_3 (and_3_out, nor_1_out, Entrada[30]);
  or or_2 (Salida[30], and_1_out, and_3_out, and_20_out);
  and and_4 (and_4_out, Entrada[30], SRA1);
  and and_5 (and_5_out, nor_1_out, Entrada[29]);
  or or_3 (Salida[29], and_4_out, and_5_out, and_23_out);
  and and_6 (and_6_out, Entrada[29], SRA1);
  and and_7 (and_7_out, nor_1_out, Entrada[28]);
  and and_8 (and_8_out, Entrada[28], SRA1);
  or or_4 (Salida[28], and_6_out, and_7_out, and_26_out);
  and and_9 (and_9_out, nor_1_out, Entrada[27]);
  or or_5 (Salida[27], and_8_out, and_9_out, and_30_out);
  and and_10 (and_10_out, Entrada[27], SRA1);
  and and_11 (and_11_out, Entrada[26], SRA1);
  and and_12 (and_12_out, nor_1_out, Entrada[26]);
  or or_6 (Salida[26], and_10_out, and_12_out, and_33_out);
  and and_13 (and_13_out, nor_1_out, Entrada[25]);
  and and_14 (and_14_out, Entrada[25], SRA1);
  or or_7 (Salida[25], and_11_out, and_13_out, and_35_out);
  and and_15 (and_15_out, nor_1_out, Entrada[24]);
  or or_8 (Salida[24], and_14_out, and_15_out, and_38_out);
  and and_16 (and_16_out, Entrada[24], SRA1);
  and and_17 (and_17_out, nor_1_out, Entrada[23]);
  and and_18 (and_18_out, SLL8, Entrada[23]);
  or or_9 (Salida[23], and_16_out, and_17_out, and_42_out);
  and and_19 (and_19_out, SRA1, Entrada[23]);
  and and_20 (and_20_out, SLL8, Entrada[22]);
  and and_21 (and_21_out, nor_1_out, Entrada[22]);
  or or_10 (Salida[22], and_19_out, and_21_out, and_45_out);
  and and_22 (and_22_out, SRA1, Entrada[22]);
  and and_23 (and_23_out, SLL8, Entrada[21]);
  and and_24 (and_24_out, nor_1_out, Entrada[21]);
  or or_11 (Salida[21], and_22_out, and_24_out, and_48_out);
  and and_25 (and_25_out, SRA1, Entrada[21]);
  and and_26 (and_26_out, SLL8, Entrada[20]);
  and and_27 (and_27_out, nor_1_out, Entrada[20]);
  or or_12 (Salida[20], and_25_out, and_27_out, and_50_out);
  and and_28 (and_28_out, SRA1, Entrada[20]);
  and and_29 (and_29_out, nor_1_out, Entrada[19]);
  and and_30 (and_30_out, SLL8, Entrada[19]);
  or or_13 (Salida[19], and_28_out, and_29_out, and_54_out);
  and and_31 (and_31_out, SRA1, Entrada[19]);
  and and_32 (and_32_out, nor_1_out, Entrada[18]);
  and and_33 (and_33_out, SLL8, Entrada[18]);
  or or_14 (Salida[18], and_31_out, and_32_out, and_57_out);
  and and_34 (and_34_out, SRA1, Entrada[18]);
  and and_35 (and_35_out, SLL8, Entrada[17]);
  and and_36 (and_36_out, nor_1_out, Entrada[17]);
  or or_15 (Salida[17], and_34_out, and_36_out, and_59_out);
  and and_37 (and_37_out, SRA1, Entrada[17]);
  and and_38 (and_38_out, SLL8, Entrada[16]);
  and and_39 (and_39_out, nor_1_out, Entrada[16]);
  or or_16 (Salida[16], and_37_out, and_39_out, and_62_out);
  and and_40 (and_40_out, SRA1, Entrada[16]);
  and and_41 (and_41_out, nor_1_out, Entrada[15]);
  and and_42 (and_42_out, SLL8, Entrada[15]);
  or or_17 (Salida[15], and_40_out, and_41_out, and_66_out);
  and and_43 (and_43_out, SRA1, Entrada[15]);
  and and_44 (and_44_out, nor_1_out, Entrada[14]);
  and and_45 (and_45_out, SLL8, Entrada[14]);
  or or_18 (Salida[14], and_43_out, and_44_out, and_69_out);
  and and_46 (and_46_out, SRA1, Entrada[14]);
  and and_47 (and_47_out, nor_1_out, Entrada[13]);
  and and_48 (and_48_out, SLL8, Entrada[13]);
  or or_19 (Salida[13], and_46_out, and_47_out, and_72_out);
  and and_49 (and_49_out, SRA1, Entrada[13]);
  and and_50 (and_50_out, SLL8, Entrada[12]);
  and and_51 (and_51_out, nor_1_out, Entrada[12]);
  or or_20 (Salida[12], and_49_out, and_51_out, and_74_out);
  and and_52 (and_52_out, SRA1, Entrada[12]);
  and and_53 (and_53_out, nor_1_out, Entrada[11]);
  and and_54 (and_54_out, SLL8, Entrada[11]);
  or or_21 (Salida[11], and_52_out, and_53_out, and_78_out);
  and and_55 (and_55_out, SRA1, Entrada[11]);
  and and_56 (and_56_out, nor_1_out, Entrada[10]);
  and and_57 (and_57_out, SLL8, Entrada[10]);
  or or_22 (Salida[10], and_55_out, and_56_out, and_80_out);
  and and_58 (and_58_out, SRA1, Entrada[10]);
  and and_59 (and_59_out, SLL8, Entrada[9]);
  and and_60 (and_60_out, nor_1_out, Entrada[9]);
  or or_23 (Salida[9], and_58_out, and_60_out, and_83_out);
  and and_61 (and_61_out, SRA1, Entrada[9]);
  and and_62 (and_62_out, SLL8, Entrada[8]);
  and and_63 (and_63_out, nor_1_out, Entrada[8]);
  or or_24 (Salida[8], and_61_out, and_63_out, and_87_out);
  and and_64 (and_64_out, SRA1, Entrada[8]);
  and and_65 (and_65_out, nor_1_out, Entrada[7]);
  and and_66 (and_66_out, SLL8, Entrada[7]);
  or or_25 (Salida[7], and_64_out, and_65_out);
  and and_67 (and_67_out, SRA1, Entrada[7]);
  and and_68 (and_68_out, nor_1_out, Entrada[6]);
  and and_69 (and_69_out, SLL8, Entrada[6]);
  or or_26 (Salida[6], and_67_out, and_68_out);
  and and_70 (and_70_out, SRA1, Entrada[6]);
  and and_71 (and_71_out, nor_1_out, Entrada[5]);
  and and_72 (and_72_out, SLL8, Entrada[5]);
  or or_27 (Salida[5], and_70_out, and_71_out);
  and and_73 (and_73_out, SRA1, Entrada[5]);
  and and_74 (and_74_out, SLL8, Entrada[4]);
  and and_75 (and_75_out, nor_1_out, Entrada[4]);
  or or_28 (Salida[4], and_73_out, and_75_out);
  and and_76 (and_76_out, SRA1, Entrada[4]);
  and and_77 (and_77_out, nor_1_out, Entrada[3]);
  and and_78 (and_78_out, SLL8, Entrada[3]);
  or or_29 (Salida[3], and_76_out, and_77_out);
  and and_79 (and_79_out, SRA1, Entrada[3]);
  and and_80 (and_80_out, SLL8, Entrada[2]);
  and and_81 (and_81_out, nor_1_out, Entrada[2]);
  or or_30 (Salida[2], and_79_out, and_81_out);
  and and_82 (and_82_out, SRA1, Entrada[2]);
  and and_83 (and_83_out, SLL8, Entrada[1]);
  and and_84 (and_84_out, nor_1_out, Entrada[1]);
  or or_31 (Salida[1], and_82_out, and_84_out);
  and and_85 (and_85_out, SRA1, Entrada[1]);
  and and_86 (and_86_out, Entrada[0], nor_1_out);
  and and_87 (and_87_out, SLL8, Entrada[0]);
  or or_32 (Salida[0], and_85_out, and_86_out);

  // Notes on the sheet:
  //   desplazamiento logico hacia la izquierda x8
  //   desplazador aritmetico hacia la derecha x1
  //   00 no hace nada
endmodule
